# Fritzing sketch CoffeeMonitor (saved by Fritzing 0.9.3b)
circuit board: 7.54276cm x 2.71318cm
perfboards: 1

parts:
  Part1 = Photon
  J1 = male pin header, 6 pins [form="♂ (male)"]
  IC1 = IC, DIP package, 12 pins [chip_label=IC]
  J2 = male pin header, 4 pins [form="♂ (male)"]
  R1 = Resistor [tolerance=±5% resistance=4.7k package=THT]
  R2 = Resistor [tolerance=±5% resistance=4.7k package=THT]

nets:
  N1: Part1.GND, IC1.pin8, J2.pin2
  N2: Part1.D0, J2.pin4, R2.Pin_0
  N3: Part1.D1, J2.pin3, R1.Pin_0
  N4: Part1.D2, IC1.pin10
  N5: Part1.D3, IC1.pin9
  N6: Part1.3V3, IC1.pin11, J2.pin1, R1.Pin_1, R2.Pin_1
  N7: J1.pin1, IC1.pin1
  N8: J1.pin2, IC1.pin2
  N9: J1.pin3, IC1.pin3
  N10: J1.pin4, IC1.pin4
  N11: J1.pin5, IC1.pin5
  N12: J1.pin6, IC1.pin6
